# Fritzing sketch sketch (saved by Fritzing 0.7.11b)
breadboards: 1

parts:
  Down = Pushbutton [package="[THT]"]
  Right = Pushbutton [package="[THT]"]
  10k = Resistor [tolerance=±5% resistance=220 package=THT]
  10k_2 = Resistor [tolerance=±5% resistance=220 package=THT]
  Arduino1 = Arduino
  Left = Pushbutton [package="[THT]"]
  10k_3 = Resistor [tolerance=±5% resistance=10k package=THT]
  Up = Pushbutton [package="[THT]"]
  10k_4 = Resistor [tolerance=±5% resistance=220 package=THT]
  10k_5 = Resistor [tolerance=±5% resistance=220 package=THT]
  4_7k = Resistor [tolerance=±5% resistance=220 package=THT]
  DS18 = screw terminal, 3 pins
  LCD1 = LCD screen
  POT = Trimmer Potentiometer [maximum_resistance=10kΩ package=THT]
  Reset = Pushbutton [package="[THT]"]
  SSR = Screw terminal - 2 pins [package=THT]
  LED1 = LED - 5mm [color="Red (633nm)" package="5 mm [THT]"]
  R1 = Resistor [tolerance=±5% resistance=220 package=THT]

nets:
  N1: Down.Pin_1, Down.Pin_2, Arduino1.D10, 10k_4.Pin_1
  +5V: Down.Pin_3, Down.Pin_4, Right.Pin_3, Right.Pin_4, Arduino1.+5V, Left.Pin_3, Left.Pin_4, Up.Pin_3, Up.Pin_4, 4_7k.Pin_0, DS18.pin1, LCD1.VDD, LCD1.LED+, POT.leg2, LED1.anode
  N2: Right.Pin_1, Right.Pin_2, 10k_2.Pin_1, Arduino1.D2
  GND: 10k.Pin_0, 10k_2.Pin_0, Arduino1.GND, 10k_3.Pin_0, 10k_4.Pin_0, 10k_5.Pin_1, DS18.pin3, LCD1.VSS, LCD1.R/W, LCD1.LED-, POT.leg1, Reset.Pin_1, Reset.Pin_2, R1.Pin_1
  N3: 10k.Pin_1, Arduino1.D3, Left.Pin_1, Left.Pin_2
  N4: Arduino1.D13, LCD1.RS
  N5: Arduino1.D12, LCD1.E
  N6: Arduino1.D11, 10k_3.Pin_1, Up.Pin_1, Up.Pin_2
  N7: Arduino1.D9, SSR.pin1
  N8: Arduino1.D8, 4_7k.Pin_1, DS18.pin2
  N9: Arduino1.D7, LCD1.DB4
  N10: Arduino1.D6, LCD1.DB5
  N11: Arduino1.D5, LCD1.DB6
  N12: Arduino1.D4, LCD1.DB7
  N13: Arduino1.RST, Reset.Pin_3, Reset.Pin_4
  N14: 10k_5.Pin_0, SSR.pin2
  N15: LCD1.V0, POT.wiper
  N16: LED1.cathode, R1.Pin_0

notes:
  DS18
  SSR
  5v
  Gnd
  Bus
  +
  -
  thermoshield v0.1
  kerinin@gmail.com
  Pwr
  RX0
  TX1
  A5
  A4
  A3
  A2
  A1
  A0
  Vin
  3v
  Rst
  V0
  RS
  E
  DB4
  DB5
  DB6
  DB7
  13
  12
  ~11
  ~10
  ~9
  8
  7
  ~6
  ~5
  4
  ~3
  2
